# Fritzing sketch kemar projectyy (saved by Fritzing 0.9.3b)
circuit board: 5.56292cm x 2.92599cm
breadboards: 1

parts:
  Raspberry_Pi_1 = Raspberry Pi 3 [part_number=RPI-3-V1.2]
  HT16K33 = female pin header, 4 pins [form="♀ (female)"]

nets:
  N1: Raspberry_Pi_1.GPIO2, HT16K33.pin2
  N2: Raspberry_Pi_1.GPIO3, HT16K33.pin1
  N3: Raspberry_Pi_1.GND, HT16K33.pin3
  N4: Raspberry_Pi_1.5V, HT16K33.pin4

notes:
  Kemar Carnegie
